# Fritzing sketch OpenMQTTGateway (saved by Fritzing 0.9.3b)
circuit board: 10cm x 6cm
breadboards: 1

parts:
  C1 = Electrolytic Capacitor [capacitance=10µF package="100 mil [THT, electrolytic]"]
  R1 = Resistor [tolerance=±5% resistance=1k package=THT]
  D1 = Rectifier Diode [part_number=1N4001 package="300 mil [THT]"]
  J1 = Screw terminal - 2 pins [package=THT]
  Componente4 = NRF24L01
  IC1 = Voltage Regulator AMS1117 [package=sot223]
  Q1 = NPN-Transistor [part_number=BC548 package="TO92 [THT]"]
  R2 = Resistor [tolerance=±5% resistance=1k package=THT]
  D2 = Rectifier Diode [part_number=1N4001 package="300 mil [THT]"]
  Q2 = NPN-Transistor [part_number=BC548 package="TO92 [THT]"]
  Q3 = NPN-Transistor [part_number=BC548 package="TO92 [THT]"]
  R3 = Resistor [tolerance=±5% resistance=1k package=THT]
  D3 = Rectifier Diode [part_number=1N4001 package="300 mil [THT]"]
  T1 = LM35 Temperature Sensor [package="TO92 [THT]"]
  J2 = screw terminal, 3 pins
  J3 = screw terminal, 3 pins
  J4 = screw terminal, 3 pins
  OMRON1 = OMRON PCB Power Relay – G5LE [part_number="G5LE-1\n" package=THT]
  OMRON3 = OMRON PCB Power Relay – G5LE [part_number="G5LE-1\n" package=THT]
  OMRON2 = OMRON PCB Power Relay – G5LE [part_number="G5LE-1\n" package=THT]
  RFTX = mystery part, 3 pins [chip_label="RF433 TX"]
  RFRX = mystery part, 4 pins [chip_label="RF433 RX"]
  Componente3 = Arduino Pro Mini v13
  WeMos_D1_Mini1 = WeMos D1 Mini

nets:
  GND: C1.-, J1.pin1, Componente4.GND, IC1.GND, Q1.E, Q2.E, Q3.E, T1.GND, RFTX.pin3, RFRX.pin4, Componente3.GND
  N1: C1.+, Componente4.VCC, IC1.OUT
  N2: R1.Pin_0, Componente3.D6_PWM, WeMos_D1_Mini1.D6
  N3: R1.Pin_1, Q1.B
  5V: D1.cathode, J1.pin2, IC1.IN, D2.cathode, D3.cathode, T1.+Vs, OMRON1.COIL1, OMRON3.COIL1, OMRON2.COIL1, RFTX.pin2, RFRX.pin1, Componente3.VCC
  N4: D1.anode, Q1.C, OMRON2.COIL2
  N5: Componente4.MOSI, Componente3.D11_PWM/MOSI
  N6: Componente4.CSN, Componente3.D10_PWM/SS
  N7: Componente4.MISO, Componente3.D12/MISO
  N8: Componente4.SCK, Componente3.D13/SCK
  N9: Componente4.CE, Componente3.D9_PWM
  N10: R2.Pin_0, Componente3.D5_PWM, WeMos_D1_Mini1.D5
  N11: R2.Pin_1, Q2.B
  N12: D2.anode, Q2.C, OMRON1.COIL2
  N13: Q3.B, R3.Pin_1
  N14: Q3.C, D3.anode, OMRON3.COIL2
  N15: R3.Pin_0, Componente3.D7, WeMos_D1_Mini1.D7
  N16: T1.Vout, Componente3.A0
  N17: J2.pin1, OMRON2.B
  N18: J2.pin2, OMRON2.C
  N19: J2.pin3, OMRON2.A
  N20: J3.pin1, OMRON1.B
  N21: J3.pin2, OMRON1.C
  N22: J3.pin3, OMRON1.A
  N23: J4.pin1, OMRON3.B
  N24: J4.pin2, OMRON3.C
  N25: J4.pin3, OMRON3.A
  N26: RFTX.pin1, Componente3.D2, WeMos_D1_Mini1.RX
  N27: RFRX.pin2, Componente3.D3_PWM, WeMos_D1_Mini1.D3
